# Fritzing sketch BasicTask1-2 (saved by Fritzing 1.0.8)
breadboards: 1

parts:
  元件1 = Arduino Uno (Rev3)
  LED1 = LED - 5mm [color="Red (633nm)" current=0.030A package="5 mm [THT]"]
  S1 = Pushbutton [package="[THT]"]
  R1 = Resistor [tolerance=±5% power=0.25W resistance=1k package=THT]
  R2 = Resistor [tolerance=±5% power=0.25W resistance=220 package=THT]

nets:
  N1: 元件1.D13/SCK, R2.Pin_0
  N2: 元件1.GND, LED1.cathode, R1.Pin_0
  N3: 元件1.D2, S1.Pin_1, S1.Pin_2, R1.Pin_1
  N4: 元件1.5V, S1.Pin_3, S1.Pin_4
  N5: LED1.anode, R2.Pin_1

// code stored in the sketch: BasicTask1-1.ino
const int led_pin = 13; // BUILTIN

void setup(){
  pinMode(led_pin, 1);
}

void loop(){
  digitalWrite(led_pin, 1);
  delay(500); //500ms
  digitalWrite(led_pin, 0);
  delay(500);
}
