# Fritzing sketch BasicTask1-3 (saved by Fritzing 1.0.8)
breadboards: 1

parts:
  元件1 = Arduino Uno (Rev3)
  LED1 = LED - 5mm [color="Red (633nm)" current=0.030A package="5 mm [THT]"]
  R1 = Resistor [tolerance=±5% power=0.25W resistance=220 package=THT]

nets:
  N1: 元件1.D11_PWM/MOSI, R1.Pin_0
  N2: 元件1.GND, LED1.cathode
  N3: LED1.anode, R1.Pin_1

// code stored in the sketch: BasicTask1-1.ino
const int led_pin = 13; // BUILTIN

void setup(){
  pinMode(led_pin, 1);
}

void loop(){
  digitalWrite(led_pin, 1);
  delay(500); //500ms
  digitalWrite(led_pin, 0);
  delay(500);
}
