# Fritzing sketch Task1-2 (saved by Fritzing 1.0.8)
breadboards: 1

parts:
  元件1 = Arduino Uno (Rev3)
  R2 = 12mm Trimmer Potentiometer (Large) [maximum_resistance=10kΩ knob_status=50% power=0.5W package=THT]
  LED1 = RGB LED (com. cathode, rgb) [color="Red (633nm)" current=0.030A package="5 mm [THT]"]
  S1 = Pushbutton [package="[THT]"]
  R3 = Resistor [tolerance=±5% power=0.25W resistance=1k package=THT]

nets:
  N1: 元件1.A0, R2.wiper
  N2: 元件1.D9_PWM, LED1.blue_anode
  N3: 元件1.D10_PWM/SS, LED1.green_anode
  N4: 元件1.D11_PWM/MOSI, LED1.red_anode
  N5: 元件1.GND, R2.leg1, R3.Pin_0
  N6: 元件1.D2, S1.Pin_1, S1.Pin_2, R3.Pin_1
  N7: 元件1.5V, R2.leg2, LED1.common_cathode, S1.Pin_3, S1.Pin_4

// code stored in the sketch: BasicTask1-1.ino
const int led_pin = 13; // BUILTIN

void setup(){
  pinMode(led_pin, 1);
}

void loop(){
  digitalWrite(led_pin, 1);
  delay(500); //500ms
  digitalWrite(led_pin, 0);
  delay(500);
}
