# Fritzing sketch BasicTask1-3 (saved by Fritzing 1.0.8)
breadboards: 1

parts:
  元件1 = Arduino Uno (Rev3)
  LED1 = LED - 5mm [color="Red (633nm)" current=0.030A package="5 mm [THT]"]

nets:
  N1: 元件1.D13/SCK, LED1.anode
  N2: 元件1.GND, LED1.cathode

// code stored in the sketch: BasicTask1-1.ino
const int led_pin = 13; // BUILTIN

void setup(){
  pinMode(led_pin, 1);
}

void loop(){
  digitalWrite(led_pin, 1);
  delay(500); //500ms
  digitalWrite(led_pin, 0);
  delay(500);
}
